# Fritzing sketch multimetre (saved by Fritzing 0.9.3b)
breadboards: 3

parts:
  Composant1 = Arduino Uno (Rev3)
  J3 = LCD I2C - 4 pins [form="♀ (female)" package=THT]
  U2 = LCD-16X2 [package=lcd-16x2]  # not connected
  ChangeMode = Pushbutton [package="[THT]"]
  R2 = Resistor [tolerance=±5% resistance=1k package=THT]
  R3 = Resistor [tolerance=±5% resistance=10k package=THT]

nets:
  N1: Composant1.A0, R2.Pin_1
  N2: Composant1.A4/SDA, J3.SDA
  N3: Composant1.A5/SCL, J3.SCL
  N4: Composant1.D7, ChangeMode.Pin_1, ChangeMode.Pin_2, R3.Pin_0
  5V: Composant1.5V, J3.VCC, ChangeMode.Pin_3, ChangeMode.Pin_4
  GND: Composant1.GND, J3.GND, R2.Pin_0, R3.Pin_1

notes:
  Sonde

custom parts:
  LCD I2C - 4 pins: I2C connector for LDC
