# Fritzing sketch ohmmetre (saved by Fritzing 0.9.3b)
breadboards: 1

parts:
  Composant1 = Arduino Uno (Rev3)
  U1 = LCD-16X2 [package=lcd-16x2]  # not connected
  R1 = Resistor [tolerance=±5% resistance=1k package=THT]  # not connected
  R2 = Resistor [tolerance=±5% resistance=220 package=THT]
  J2 = LCD I2C - 4 pins [form="♀ (female)" package=THT]

nets:
  N1: Composant1.A0, R2.Pin_0
  N2: Composant1.A4/SDA, J2.SDA
  N3: Composant1.A5/SCL, J2.SCL
  5V: Composant1.5V, R2.Pin_1, J2.VCC
  GND: Composant1.GND, J2.GND

notes:
  Résistance à tester

custom parts:
  LCD I2C - 4 pins: I2C connector for LDC
