# Fritzing sketch voltmetre (saved by Fritzing 0.9.3b)
breadboards: 1

parts:
  Composant1 = Arduino Uno (Rev3)
  U1 = LCD-16X2 [package=lcd-16x2]  # not connected
  R1 = Resistor [tolerance=±5% resistance=100k package=THT]
  J2 = LCD I2C - 4 pins [form="♀ (female)" package=THT]
  R2 = Resistor [tolerance=±5% resistance=10k package=THT]

nets:
  N1: Composant1.A1, R1.Pin_1, R2.Pin_0
  N2: Composant1.A4/SDA, J2.SDA
  N3: Composant1.A5/SCL, J2.SCL
  GND: Composant1.GND, J2.GND, R2.Pin_1
  5V: Composant1.5V, J2.VCC

notes:
  Sondes

custom parts:
  LCD I2C - 4 pins: I2C connector for LDC
